// Digital circuit d-latch.dig as structural Verilog
module d_latch (
  input  D,
  input  E,
  output Q,
  output Q_not
);

  wire not_1_out;

  not not_1 (not_1_out, D);
  RS_FF rs_ff_1 (.S(D), .C(E), .R(not_1_out), .Q(Q), .nQ(Q_not));
endmodule
