// Digital circuit fulladder.dig as structural Verilog
module fulladder (
  input  A,
  input  B,
  input  C,
  output Sum,
  output Carry
);

  wire and_1_out, and_2_out, and_3_out, and_4_out, and_5_out, not_1_out, or_1_out;

  and and_1 (and_1_out, A, B, C);
  or or_1 (or_1_out, A, B, C);
  and and_2 (and_2_out, A, B);
  and and_3 (and_3_out, A, C);
  and and_4 (and_4_out, B, C);
  or or_2 (Carry, and_2_out, and_3_out, and_4_out);
  and and_5 (and_5_out, or_1_out, not_1_out);
  not not_1 (not_1_out, Carry);
  or or_3 (Sum, and_1_out, and_5_out);
endmodule
