// Digital circuit halfadder.dig as structural Verilog
module halfadder (
  input  A,
  input  B,
  output Sum,
  output Carry
);

  wire not_1_out, or_1_out;

  or or_1 (or_1_out, A, B);
  and and_1 (Carry, A, B);
  not not_1 (not_1_out, Carry);
  and and_2 (Sum, or_1_out, not_1_out);
endmodule
