// Digital circuit jk-flipflop.dig as structural Verilog
module jk_flipflop (
  input  J,
  input  K,
  input  C,
  output Q,
  output Q_not
);

  wire and_1_out, and_2_out, not_1_out, rs_ff_1_nq, rs_ff_1_q;

  and and_1 (and_1_out, Q_not, J);
  and and_2 (and_2_out, K, Q);
  RS_FF rs_ff_1 (.S(and_1_out), .C(C), .R(and_2_out), .Q(rs_ff_1_q), .nQ(rs_ff_1_nq));
  not not_1 (not_1_out, C);
  RS_FF rs_ff_2 (.S(rs_ff_1_q), .C(not_1_out), .R(rs_ff_1_nq), .Q(Q), .nQ(Q_not));
endmodule
