// Digital circuit sr-flipflop.dig as structural Verilog
module sr_flipflop (
  input  Reset,
  input  Set,
  output Q,
  output Q_not
);

  nor nor_1 (Q, Reset, Q_not);
  nor nor_2 (Q_not, Q, Set);
endmodule
